# Fritzing sketch RoomAvability (saved by Fritzing 0.9.2b)

parts:
  OLED1 = 128x32 SPI Monochrome OLEDDisplay
  Raspberry_Pi3 = Raspberry Pi 2

nets:
  N1: OLED1.CS, Raspberry_Pi3.GPIO8
  N2: OLED1.RST, Raspberry_Pi3.GPIO23
  N3: OLED1.D/C, Raspberry_Pi3.GPIO22
  N4: OLED1.CLK, Raspberry_Pi3.GPIO11
  N5: OLED1.DATA, Raspberry_Pi3.GPIO10
  VIN: OLED1.VIN, Raspberry_Pi3.5V
  GND: OLED1.GND, Raspberry_Pi3.GND

custom parts:
  128x32 SPI Monochrome OLEDDisplay: 128x32 SPI OLED Monochrome Display
